// Logisim project Relógio24h.circ as structural Verilog: 9 circuits, main circuit main
module main (
);

  wire and_1_out, and_2_out, and_3_out, and_4_out, and_5_out, and_6_out, and_7_out, clock_1_out,
       display7_1_a, display7_1_b, display7_1_c, display7_1_d, display7_1_e, display7_1_f, display7_1_g,
       display7_2_a, display7_2_b, display7_2_c, display7_2_d, display7_2_e, display7_2_f, display7_2_g,
       display7_3_a, display7_3_b, display7_3_c, display7_3_d, display7_3_e, display7_3_f, display7_3_g,
       display7_4_a, display7_4_b, display7_4_c, display7_4_d, display7_4_e, display7_4_f, display7_4_g,
       display7_5_a, display7_5_b, display7_5_c, display7_5_d, display7_5_e, display7_5_f, display7_5_g,
       display7_6_a, display7_6_b, display7_6_c, display7_6_d, display7_6_e, display7_6_f, display7_6_g,
       or_1_out, t_ff_2_qn, t_ff_4_qn, t_ff_6_qn, t_ff_8_qn;
  wire [1:0] t_ff_11_q;
  wire [2:0] t_ff_9_q, t_ff_18_q;
  wire [3:0] t_ff_1_q, t_ff_2_q, t_ff_14_q;

  _7_Segment_Display u_7_segment_display_1 (
    .g(display7_1_g), .f(display7_1_f), .a(display7_1_a), .b(display7_1_b), .e(display7_1_e),
    .d(display7_1_d), .c(display7_1_c));  // open: dp
  Display7 display7_1 (
    .in_1({2'b00, t_ff_11_q}), .a(display7_1_a), .b(display7_1_b), .c(display7_1_c), .d(display7_1_d),
    .e(display7_1_e), .f(display7_1_f), .g(display7_1_g));
  _7_Segment_Display u_7_segment_display_2 (
    .g(display7_2_g), .f(display7_2_f), .a(display7_2_a), .b(display7_2_b), .e(display7_2_e),
    .d(display7_2_d), .c(display7_2_c));  // open: dp
  Display7 display7_2 (
    .in_1(t_ff_2_q), .a(display7_2_a), .b(display7_2_b), .c(display7_2_c), .d(display7_2_d),
    .e(display7_2_e), .f(display7_2_f), .g(display7_2_g));
  _7_Segment_Display u_7_segment_display_3 (
    .g(display7_3_g), .f(display7_3_f), .a(display7_3_a), .b(display7_3_b), .e(display7_3_e),
    .d(display7_3_d), .c(display7_3_c));  // open: dp
  Display7 display7_3 (
    .in_1({1'b0, t_ff_18_q}), .a(display7_3_a), .b(display7_3_b), .c(display7_3_c), .d(display7_3_d),
    .e(display7_3_e), .f(display7_3_f), .g(display7_3_g));
  _7_Segment_Display u_7_segment_display_4 (
    .g(display7_4_g), .f(display7_4_f), .a(display7_4_a), .b(display7_4_b), .e(display7_4_e),
    .d(display7_4_d), .c(display7_4_c));  // open: dp
  Display7 display7_4 (
    .in_1(t_ff_14_q), .a(display7_4_a), .b(display7_4_b), .c(display7_4_c), .d(display7_4_d),
    .e(display7_4_e), .f(display7_4_f), .g(display7_4_g));
  _7_Segment_Display u_7_segment_display_5 (
    .g(display7_5_g), .f(display7_5_f), .a(display7_5_a), .b(display7_5_b), .e(display7_5_e),
    .d(display7_5_d), .c(display7_5_c));  // open: dp
  Display7 display7_5 (
    .in_1({1'b0, t_ff_9_q}), .a(display7_5_a), .b(display7_5_b), .c(display7_5_c), .d(display7_5_d),
    .e(display7_5_e), .f(display7_5_f), .g(display7_5_g));
  _7_Segment_Display u_7_segment_display_6 (
    .g(display7_6_g), .f(display7_6_f), .a(display7_6_a), .b(display7_6_b), .e(display7_6_e),
    .d(display7_6_d), .c(display7_6_c));  // open: dp
  Display7 display7_6 (
    .in_1(t_ff_1_q), .a(display7_6_a), .b(display7_6_b), .c(display7_6_c), .d(display7_6_d),
    .e(display7_6_e), .f(display7_6_f), .g(display7_6_g));
  Clock clock_1 (.out(clock_1_out));
  T_Flip_Flop #(.trigger("falling")) t_ff_1 (
    .clk(clock_1_out), .T(1'b1), .Q(t_ff_1_q[0]), .reset(and_1_out));  // open: Qn, preset, en
  T_Flip_Flop #(.trigger("falling")) t_ff_2 (
    .clk(and_7_out), .T(1'b1), .Q(t_ff_2_q[0]), .Qn(t_ff_2_qn), .reset(or_1_out));  // open: preset, en
  T_Flip_Flop #(.trigger("falling")) t_ff_3 (
    .clk(t_ff_1_q[0]), .T(1'b1), .Q(t_ff_1_q[1]), .reset(and_1_out));  // open: Qn, preset, en
  and and_1 (and_1_out, ~t_ff_1_q[0], t_ff_1_q[1], ~t_ff_1_q[2], t_ff_1_q[3]);  // AND_Gate
  T_Flip_Flop #(.trigger("falling")) t_ff_4 (
    .clk(t_ff_2_q[0]), .T(1'b1), .Q(t_ff_2_q[1]), .Qn(t_ff_4_qn), .reset(or_1_out));  // open: preset, en
  T_Flip_Flop #(.trigger("falling")) t_ff_5 (
    .clk(t_ff_1_q[1]), .T(1'b1), .Q(t_ff_1_q[2]), .reset(and_1_out));  // open: Qn, preset, en
  T_Flip_Flop #(.trigger("falling")) t_ff_6 (
    .clk(t_ff_2_q[1]), .T(1'b1), .Q(t_ff_2_q[2]), .Qn(t_ff_6_qn), .reset(or_1_out));  // open: preset, en
  and and_2 (and_2_out, ~t_ff_2_q[0], t_ff_2_q[1], ~t_ff_2_q[2], t_ff_2_q[3]);  // AND_Gate
  T_Flip_Flop #(.trigger("falling")) t_ff_7 (
    .clk(t_ff_1_q[2]), .T(1'b1), .Q(t_ff_1_q[3]), .reset(and_1_out));  // open: Qn, preset, en
  T_Flip_Flop #(.trigger("falling")) t_ff_8 (
    .clk(t_ff_2_q[2]), .T(1'b1), .Q(t_ff_2_q[3]), .Qn(t_ff_8_qn), .reset(or_1_out));  // open: preset, en
  or or_1 (or_1_out, and_2_out, and_5_out);
  T_Flip_Flop #(.trigger("falling")) t_ff_9 (
    .clk(and_1_out), .T(1'b1), .Q(t_ff_9_q[0]), .reset(and_3_out));  // open: Qn, preset, en
  and and_3 (and_3_out, ~t_ff_9_q[0], t_ff_9_q[1], t_ff_9_q[2]);  // AND_Gate
  and and_4 (and_4_out, ~t_ff_8_qn, t_ff_6_qn, ~t_ff_4_qn, t_ff_2_qn);  // AND_Gate
  and and_5 (and_5_out, t_ff_2_q[2], t_ff_11_q[1]);
  T_Flip_Flop #(.trigger("falling")) t_ff_10 (
    .clk(t_ff_9_q[0]), .T(1'b1), .Q(t_ff_9_q[1]), .reset(and_3_out));  // open: Qn, preset, en
  T_Flip_Flop #(.trigger("falling")) t_ff_11 (
    .clk(and_4_out), .T(1'b1), .Q(t_ff_11_q[0]), .reset(and_5_out));  // open: Qn, preset, en
  T_Flip_Flop #(.trigger("falling")) t_ff_12 (
    .clk(t_ff_9_q[1]), .T(1'b1), .Q(t_ff_9_q[2]), .reset(and_3_out));  // open: Qn, preset, en
  T_Flip_Flop #(.trigger("falling")) t_ff_13 (
    .clk(t_ff_11_q[0]), .T(1'b1), .Q(t_ff_11_q[1]), .reset(and_5_out));  // open: Qn, preset, en
  T_Flip_Flop #(.trigger("falling")) t_ff_14 (
    .clk(and_3_out), .T(1'b1), .Q(t_ff_14_q[0]), .reset(and_6_out));  // open: Qn, preset, en
  and and_6 (and_6_out, ~t_ff_14_q[0], t_ff_14_q[1], ~t_ff_14_q[2], t_ff_14_q[3]);  // AND_Gate
  T_Flip_Flop #(.trigger("falling")) t_ff_15 (
    .clk(t_ff_14_q[0]), .T(1'b1), .Q(t_ff_14_q[1]), .reset(and_6_out));  // open: Qn, preset, en
  T_Flip_Flop #(.trigger("falling")) t_ff_16 (
    .clk(t_ff_14_q[1]), .T(1'b1), .Q(t_ff_14_q[2]), .reset(and_6_out));  // open: Qn, preset, en
  T_Flip_Flop #(.trigger("falling")) t_ff_17 (
    .clk(t_ff_14_q[2]), .T(1'b1), .Q(t_ff_14_q[3]), .reset(and_6_out));  // open: Qn, preset, en
  T_Flip_Flop #(.trigger("falling")) t_ff_18 (
    .clk(and_6_out), .T(1'b1), .Q(t_ff_18_q[0]), .reset(and_7_out));  // open: Qn, preset, en
  and and_7 (and_7_out, ~t_ff_18_q[0], t_ff_18_q[1], t_ff_18_q[2]);  // AND_Gate
  T_Flip_Flop #(.trigger("falling")) t_ff_19 (
    .clk(t_ff_18_q[0]), .T(1'b1), .Q(t_ff_18_q[1]), .reset(and_7_out));  // open: Qn, preset, en
  T_Flip_Flop #(.trigger("falling")) t_ff_20 (
    .clk(t_ff_18_q[1]), .T(1'b1), .Q(t_ff_18_q[2]), .reset(and_7_out));  // open: Qn, preset, en

  // Notes on the sheet:
  //   Artur Pigari Prata - 2101297
  //   Horas
  //   Minutos
  //   Segundos
endmodule

module Display7 (
  input  [3:0] in_1,
  output a,
  output b,
  output c,
  output d,
  output e,
  output f,
  output g
);

  Segmento_a segmento_a_1 (.in_1(in_1), .a(a));
  Segmento_b segmento_b_1 (.in_1(in_1), .b(b));
  Segmento_c segmento_c_1 (.in_1(in_1), .c(c));
  Segmento_d segmento_d_1 (.in_1(in_1), .d(d));
  Segmento_e segmento_e_1 (.in_1(in_1), .e(e));
  Segmento_f segmento_f_1 (.in_1(in_1), .f(f));
  Segmento_g segmento_g_1 (.in_1(in_1), .g(g));
endmodule

module Segmento_a (
  input  [3:0] in_1,
  output a
);

  wire and_1_out, and_2_out, and_3_out, and_4_out;

  and and_1 (and_1_out, ~in_1[3], ~in_1[2], ~in_1[0]);  // AND_Gate
  and and_2 (and_2_out, ~in_1[3], in_1[1]);  // AND_Gate
  and and_3 (and_3_out, ~in_1[3], in_1[2], in_1[0]);  // AND_Gate
  and and_4 (and_4_out, in_1[3], ~in_1[2], ~in_1[1]);  // AND_Gate
  or or_1 (a, and_1_out, and_2_out, and_3_out, and_4_out);
endmodule

module Segmento_b (
  input  [3:0] in_1,
  output b
);

  wire and_1_out, and_2_out, and_3_out, and_4_out;

  and and_1 (and_1_out, ~in_1[3], ~in_1[2]);  // AND_Gate
  and and_2 (and_2_out, ~in_1[3], ~in_1[1], ~in_1[0]);  // AND_Gate
  and and_3 (and_3_out, ~in_1[2], ~in_1[1]);  // AND_Gate
  and and_4 (and_4_out, ~in_1[3], in_1[1], in_1[0]);  // AND_Gate
  or or_1 (b, and_1_out, and_2_out, and_3_out, and_4_out);
endmodule

module Segmento_c (
  input  [3:0] in_1,
  output c
);

  wire and_1_out, and_2_out, and_3_out;

  and and_1 (and_1_out, ~in_1[2], ~in_1[1]);  // AND_Gate
  and and_2 (and_2_out, ~in_1[3], in_1[0]);  // AND_Gate
  and and_3 (and_3_out, ~in_1[3], in_1[2]);  // AND_Gate
  or or_1 (c, and_1_out, and_2_out, and_3_out);
endmodule

module Segmento_d (
  input  [3:0] in_1,
  output d
);

  wire and_1_out, and_2_out, and_3_out, and_4_out, and_5_out;

  and and_1 (and_1_out, ~in_1[3], ~in_1[2], ~in_1[0]);  // AND_Gate
  and and_2 (and_2_out, ~in_1[3], ~in_1[2], in_1[1]);  // AND_Gate
  and and_3 (and_3_out, ~in_1[3], in_1[1], ~in_1[0]);  // AND_Gate
  and and_4 (and_4_out, ~in_1[3], in_1[2], ~in_1[1], in_1[0]);  // AND_Gate
  and and_5 (and_5_out, in_1[3], ~in_1[2], ~in_1[1]);  // AND_Gate
  or or_1 (d, and_1_out, and_2_out, and_3_out, and_4_out, and_5_out);
endmodule

module Segmento_e (
  input  [3:0] in_1,
  output e
);

  wire and_1_out, and_2_out, and_3_out;

  and and_1 (and_1_out, ~in_1[3], ~in_1[2], ~in_1[0]);  // AND_Gate
  and and_2 (and_2_out, ~in_1[2], ~in_1[1], ~in_1[0]);  // AND_Gate
  and and_3 (and_3_out, ~in_1[3], in_1[1], ~in_1[0]);  // AND_Gate
  or or_1 (e, and_1_out, and_2_out, and_3_out);
endmodule

module Segmento_f (
  input  [3:0] in_1,
  output f
);

  wire and_1_out, and_2_out, and_3_out, and_4_out;

  and and_1 (and_1_out, ~in_1[3], ~in_1[1], ~in_1[0]);  // AND_Gate
  and and_2 (and_2_out, ~in_1[3], in_1[2], ~in_1[1]);  // AND_Gate
  and and_3 (and_3_out, ~in_1[3], in_1[2], ~in_1[0]);  // AND_Gate
  and and_4 (and_4_out, in_1[3], ~in_1[2], ~in_1[1]);  // AND_Gate
  or or_1 (f, and_1_out, and_2_out, and_3_out, and_4_out);
endmodule

module Segmento_g (
  input  [3:0] in_1,
  output g
);

  wire and_1_out, and_2_out, and_3_out, and_4_out;

  and and_1 (and_1_out, ~in_1[3], ~in_1[2], in_1[1]);  // AND_Gate
  and and_2 (and_2_out, ~in_1[3], in_1[2], ~in_1[1]);  // AND_Gate
  and and_3 (and_3_out, ~in_1[3], in_1[2], ~in_1[0]);  // AND_Gate
  and and_4 (and_4_out, in_1[3], ~in_1[2], ~in_1[1]);  // AND_Gate
  or or_1 (g, and_1_out, and_2_out, and_3_out, and_4_out);
endmodule
